// Logisim project tennis.circ as structural Verilog
module main (
  input  [2:0] in_1,
  input  [4:0] in_2,
  input  [4:0] in_3,
  input  [4:0] in_4,
  input  [4:0] in_5,
  output [7:0] out_6
);

  wire and_2_out, cdm_8_mark5_1_p9, cdm_8_mark5_1_p10, cdm_8_mark5_1_p11, cdm_8_mark5_1_p12,
       cdm_8_mark5_1_p13, clk, decoder_1_out0, decoder_1_out1, IAck, IOsel, IRQ, not_1_out, not_2_out,
       READwrite, reset, undriven;
  wire [1:0] joystick_1_y;
  wire [2:0] vec;
  wire [3:0] IOaddr;
  wire [4:0] kinematic_controller_1_p9, kinematic_controller_1_p10, kinematic_controller_1_p11,
       kinematic_controller_1_p12, kinematic_controller_1_p13, x_ball, y_ball;
  wire [7:0] cdm8_score, cdm_8_mark5_1_p16, cdm_8_mark5_1_p17, counter_1_q, multiplexer_2_out,
       multiplexer_3_out, player_score, undriven_2, undriven_3, x, y;
  wire [7:4] cdm_8_mark5_1_p15;
  wire [31:0] video_system_1_out_6, video_system_1_out_7, video_system_1_out_8, video_system_1_out_9,
       video_system_1_out_10, video_system_1_out_11, video_system_1_out_12, video_system_1_out_13,
       video_system_1_out_14, video_system_1_out_15, video_system_1_out_16, video_system_1_out_17,
       video_system_1_out_18, video_system_1_out_19, video_system_1_out_20, video_system_1_out_21,
       video_system_1_out_22, video_system_1_out_23, video_system_1_out_24, video_system_1_out_25,
       video_system_1_out_26, video_system_1_out_27, video_system_1_out_28, video_system_1_out_29,
       video_system_1_out_30, video_system_1_out_31, video_system_1_out_32, video_system_1_out_33,
       video_system_1_out_34, video_system_1_out_35, video_system_1_out_36, video_system_1_out_37;

  Counter counter_1 (.load(undriven), .Q(counter_1_q));  // open: D, count, carry, clk, clr
  Multiplexer #(.width(8)) multiplexer_1 (.in0(undriven_2), .in1(undriven_3));  // open: out, sel, en
  Adder adder_1 (.a(8'hf0), .b(counter_1_q));  // open: out, cin, cout
  Joystick #(.bits(2)) joystick_1 (.y(joystick_1_y));  // open: x
  Bit_Extender #(.out_width(5)) bit_extender_1 (.in(y), .out(y_ball));
  Bit_Extender #(.out_width(5)) bit_extender_2 (.in(x), .out(x_ball));
  LED led_1 ();  // open: in
  LED led_2 ();  // open: in
  LED led_3 ();  // open: in
  LED led_4 ();  // open: in
  Hex_Digit_Display hex_digit_display_1 ();  // open: value, dp
  // score_main main_1: pin names not known; wires that end beside it: in_1, player_score
  LED led_5 ();  // open: in
  LED led_6 ();  // open: in
  LED led_7 ();  // open: in
  LED led_8 ();  // open: in
  Hex_Digit_Display hex_digit_display_2 ();  // open: value, dp
  video_system video_system_1 (
    .in_1(kinematic_controller_1_p9), .in_2(kinematic_controller_1_p10), .in_3(kinematic_controller_1_p11),
    .in_4(kinematic_controller_1_p12), .in_5(kinematic_controller_1_p13), .out_6(video_system_1_out_6),
    .out_14(video_system_1_out_14), .out_7(video_system_1_out_7), .out_22(video_system_1_out_22),
    .out_15(video_system_1_out_15), .out_30(video_system_1_out_30), .out_8(video_system_1_out_8),
    .out_23(video_system_1_out_23), .out_16(video_system_1_out_16), .out_31(video_system_1_out_31),
    .out_9(video_system_1_out_9), .out_24(video_system_1_out_24), .out_17(video_system_1_out_17),
    .out_32(video_system_1_out_32), .out_10(video_system_1_out_10), .out_25(video_system_1_out_25),
    .out_18(video_system_1_out_18), .out_33(video_system_1_out_33), .out_11(video_system_1_out_11),
    .out_26(video_system_1_out_26), .out_19(video_system_1_out_19), .out_34(video_system_1_out_34),
    .out_12(video_system_1_out_12), .out_27(video_system_1_out_27), .out_20(video_system_1_out_20),
    .out_35(video_system_1_out_35), .out_13(video_system_1_out_13), .out_28(video_system_1_out_28),
    .out_21(video_system_1_out_21), .out_36(video_system_1_out_36), .out_29(video_system_1_out_29),
    .out_37(video_system_1_out_37));
  DotMatrix #(.matrixcols(32), .matrixrows(32)) dotmatrix_1 (
    .col0(video_system_1_out_6), .col1(video_system_1_out_7), .col2(video_system_1_out_8),
    .col3(video_system_1_out_9), .col4(video_system_1_out_10), .col5(video_system_1_out_11),
    .col6(video_system_1_out_12), .col7(video_system_1_out_13), .col8(video_system_1_out_14),
    .col9(video_system_1_out_15), .col10(video_system_1_out_16), .col11(video_system_1_out_17),
    .col12(video_system_1_out_18), .col13(video_system_1_out_19), .col14(video_system_1_out_20),
    .col15(video_system_1_out_21), .col16(video_system_1_out_22), .col17(video_system_1_out_23),
    .col18(video_system_1_out_24), .col19(video_system_1_out_25), .col20(video_system_1_out_26),
    .col21(video_system_1_out_27), .col22(video_system_1_out_28), .col23(video_system_1_out_29),
    .col24(video_system_1_out_30), .col25(video_system_1_out_31), .col26(video_system_1_out_32),
    .col27(video_system_1_out_33), .col28(video_system_1_out_34), .col29(video_system_1_out_35),
    .col30(video_system_1_out_36), .col31(video_system_1_out_37));
  // kinematic_controller kinematic_controller_1: pin names not known; wires that end beside it: joystick_1_y, in_2, in_3, in_4, in_5, 1'b1, 1'b0, reset, kinematic_controller_1_p9, kinematic_controller_1_p10, kinematic_controller_1_p11, kinematic_controller_1_p12, kinematic_controller_1_p13
  Clock clock_1 (.out(clk));
  LED led_9 ();  // open: in
  LED led_10 ();  // open: in
  LED led_11 ();  // open: in
  LED led_12 ();  // open: in
  // Probe on cdm8_score
  // Probe on player_score
  // Probe on y
  // Probe on x
  // Probe on cdm_8_mark5_1_p9
  LED led_13 ();  // open: in
  LED led_14 ();  // open: in
  LED led_15 ();  // open: in
  LED led_16 ();  // open: in
  and and_1 (IOsel, cdm_8_mark5_1_p15[4], cdm_8_mark5_1_p15[5], cdm_8_mark5_1_p15[6], cdm_8_mark5_1_p15[7], decoder_1_out1);
  // Probe on cdm_8_mark5_1_p10
  // Probe on cdm_8_mark5_1_p11
  // CdM_8_mark5 cdm_8_mark5_1: pin names not known; wires that end beside it: IRQ, vec, IAck, x, y, clk, player_score, cdm8_score, cdm_8_mark5_1_p9, cdm_8_mark5_1_p10, cdm_8_mark5_1_p11, cdm_8_mark5_1_p12, cdm_8_mark5_1_p13, READwrite, {cdm_8_mark5_1_p15, IOaddr}, cdm_8_mark5_1_p16, cdm_8_mark5_1_p17
  LED led_17 ();  // open: in
  LED led_18 ();  // open: in
  LED led_19 ();  // open: in
  LED led_20 ();  // open: in
  Decoder #(.disabled(0)) decoder_1 (
    .out0(decoder_1_out0), .out1(decoder_1_out1), .sel(cdm_8_mark5_1_p12), .en(cdm_8_mark5_1_p13));
  not not_1 (not_1_out, READwrite);
  assign out_6 = not_1_out ? cdm_8_mark5_1_p16 : 8'bz;  // Controlled_Buffer controlled_buffer_1
  assign cdm_8_mark5_1_p17 = READwrite ? out_6 : 8'bz;  // Controlled_Buffer controlled_buffer_2
  LED led_21 ();  // open: in
  LED led_22 ();  // open: in
  LED led_23 ();  // open: in
  LED led_24 ();  // open: in
  // score_main main_2: pin names not known; wires that end beside it: cdm8_score
  Hex_Digit_Display hex_digit_display_3 ();  // open: value, dp
  // Probe on {cdm_8_mark5_1_p15, IOaddr}
  and and_2 (and_2_out, decoder_1_out1, ~IOsel);  // AND_Gate
  LED led_25 ();  // open: in
  LED led_26 ();  // open: in
  LED led_27 ();  // open: in
  LED led_28 ();  // open: in
  Hex_Digit_Display hex_digit_display_4 ();  // open: value, dp
  Multiplexer #(.width(8)) multiplexer_2 (.out(multiplexer_2_out));  // open: in0, in1, sel, en
  LED led_29 ();  // open: in
  LED led_30 ();  // open: in
  LED led_31 ();  // open: in
  LED led_32 ();  // open: in
  Button u_Reset (.out(reset));
  // Probe on out_6
  Multiplexer #(.width(8)) multiplexer_3 (.out(multiplexer_3_out));  // open: in0, in1, sel, en
  not not_2 (not_2_out, clk);
  RAM #(.bus("separate")) ram_1 (
    .addr(multiplexer_2_out), .din(multiplexer_3_out), .data(out_6), .sel(and_2_out), .clk(not_2_out),
    .ld(READwrite));  // open: str, clr
  ROM rom_1 (.addr({cdm_8_mark5_1_p15, IOaddr}), .data(out_6), .sel(decoder_1_out0));

  // Other names for the same wires on the sheet: IOdat[7:0] = out_6

  // Notes on the sheet:
  //   contents of rom_1 (hex, n*v repeats v):
  //   d6 2 d0 f2 b0 d1 e4 b5 71 e1 12 d0 f0 b0 8c d3 f0 ac d1 e5 b5 71 e1 1f d0 f1 b0 8c d3 f1 ac d7 d4
  //   193*0 ff 1e 1f 11*0 1 1
endmodule

module decoder7_seg_ind (
  input  in_1,
  input  in_2,
  input  _1,
  input  _0,
  output a,
  output b,
  output f,
  output c,
  output d,
  output e,
  output g
);

  wire and_1_out, and_2_out, and_3_out, and_4_out, and_5_out, and_6_out, and_7_out, and_8_out, and_9_out,
       and_10_out, and_11_out, and_12_out, and_13_out, not_1_out, not_2_out, not_3_out, not_4_out, or_1_out,
       or_2_out, or_3_out, or_4_out, or_5_out;

  or or_1 (or_1_out, and_2_out, and_1_out);
  and and_1 (and_1_out, in_2, not_4_out);
  and and_2 (and_2_out, not_2_out, _0);
  nand nand_1 (a, not_3_out, not_1_out, or_1_out);
  and and_3 (and_3_out, not_3_out, _0);
  nand nand_2 (b, in_2, not_1_out, or_2_out);
  or or_2 (or_2_out, and_3_out, and_4_out);
  and and_4 (and_4_out, _1, not_4_out);
  nand nand_3 (f, not_1_out, or_3_out);
  or or_3 (or_3_out, and_5_out, and_6_out);
  and and_5 (and_5_out, or_2_out, not_2_out);
  and and_6 (and_6_out, _1, _0);
  not not_1 (not_1_out, in_1);
  nand nand_4 (c, not_1_out, not_2_out, _1, not_4_out);
  not not_2 (not_2_out, in_2);
  not not_3 (not_3_out, _1);
  and and_7 (and_7_out, in_2, _1, _0);
  not not_4 (not_4_out, _0);
  nand nand_5 (d, not_1_out, or_4_out);
  or or_4 (or_4_out, and_7_out, and_9_out, and_8_out);
  and and_8 (and_8_out, not_2_out, not_3_out, _0);
  and and_9 (and_9_out, in_2, not_3_out, not_4_out);
  nor nor_1 (e, and_8_out, and_10_out, and_11_out);
  and and_10 (and_10_out, not_1_out, _1, _0);
  and and_11 (and_11_out, not_1_out, in_2, not_3_out);
  nand nand_6 (g, not_1_out, or_5_out);
  or or_5 (or_5_out, and_12_out, and_13_out);
  and and_12 (and_12_out, in_2, _1, _0);
  and and_13 (and_13_out, not_2_out, not_3_out);
endmodule

module dial (
  input  [5:0] in_1,
  output out_2,
  output out_3,
  output out_4,
  output out_5,
  output out_6,
  output out_7,
  output out_8,
  output out_9,
  output out_10,
  output out_11,
  output out_12,
  output out_13,
  output out_14,
  output out_15
);

  wire [3:0] bit_extender_1_out, bit_extender_2_out;
  wire [5:0] divider_1_out, divider_1_rem;

  Divider #(.width(6)) divider_1 (.a(in_1), .b(6'b001010), .out(divider_1_out), .rem(divider_1_rem));  // open: upper
  Bit_Extender #(.in_width(6), .out_width(4)) bit_extender_1 (.in(divider_1_out), .out(bit_extender_1_out));
  Bit_Extender #(.in_width(6), .out_width(4)) bit_extender_2 (.in(divider_1_rem), .out(bit_extender_2_out));
  decoder7_seg_ind decoder7_seg_ind_1 (
    .a(out_2), .b(out_3), .f(out_7), .c(out_4), .d(out_5), .e(out_6), .g(out_8),
    .in_1(bit_extender_1_out[3]), .in_2(bit_extender_1_out[2]), ._1(bit_extender_1_out[1]),
    ._0(bit_extender_1_out[0]));
  decoder7_seg_ind decoder7_seg_ind_2 (
    .a(out_9), .b(out_10), .f(out_14), .c(out_11), .d(out_12), .e(out_13), .g(out_15),
    .in_1(bit_extender_2_out[3]), .in_2(bit_extender_2_out[2]), ._1(bit_extender_2_out[1]),
    ._0(bit_extender_2_out[0]));
endmodule

module video_chip (
  input  [4:0] chipID,
  input  [4:0] ballX,
  input  [4:0] ballY,
  input  [4:0] leftBat,
  input  [4:0] rightBat,
  output [4:0] nextChipID,
  output [4:0] ballX_2,
  output [4:0] ballY_2,
  output [4:0] leftBat_2,
  output [4:0] rightBat_2
);

  inc inc_1 (.in_1(chipID), .out_2(nextChipID));

  assign ballX_2 = ballX;
  assign ballY_2 = ballY;
  assign leftBat_2 = leftBat;
  assign rightBat_2 = rightBat;
endmodule

module inc (
  input  [4:0] in_1,
  output [4:0] out_2
);

  wire [4:0] and_1_out;

  assign and_1_out = {and_1_out[3:0], 1'b1} & in_1;  // AND_Gate and_1, 5 bits wide
  assign out_2 = in_1 ^ {and_1_out[3:0], 1'b1};  // XOR_Gate xor_1, 5 bits wide
  // also tied to GND on the sheet: and_1_out[4]
endmodule

module video_section (
  input  [4:0] in_1,
  input  [4:0] in_2,
  input  [4:0] in_3,
  input  [4:0] in_4,
  input  [4:0] in_5,
  output [31:0] out_6,
  output [31:0] out_7,
  output [31:0] out_8,
  output [31:0] out_9,
  output [31:0] out_10,
  output [31:0] out_11,
  output [31:0] out_12,
  output [31:0] out_13,
  output [4:0] out_14,
  output [4:0] out_15,
  output [4:0] out_16,
  output [4:0] out_17,
  output [4:0] out_18
);

  wire comparator_1_eq, comparator_2_eq, comparator_3_eq, comparator_4_eq, comparator_5_eq, comparator_6_eq,
       comparator_7_eq, comparator_8_eq, comparator_9_eq, comparator_10_eq, not_1_out, not_2_out;
  wire [4:0] ID1, ID2, ID3, ID4, ID5, ID6, ID7, video_chip_1_ballx_2, video_chip_1_bally_2,
       video_chip_1_leftbat_2, video_chip_1_rightbat_2, video_chip_2_ballx_2, video_chip_2_bally_2,
       video_chip_2_leftbat_2, video_chip_2_rightbat_2, video_chip_3_ballx_2, video_chip_3_bally_2,
       video_chip_3_leftbat_2, video_chip_3_rightbat_2, video_chip_4_ballx_2, video_chip_4_bally_2,
       video_chip_4_leftbat_2, video_chip_4_rightbat_2, video_chip_5_ballx_2, video_chip_5_bally_2,
       video_chip_5_leftbat_2, video_chip_5_rightbat_2, video_chip_6_ballx_2, video_chip_6_bally_2,
       video_chip_6_leftbat_2, video_chip_6_rightbat_2, video_chip_7_ballx_2, video_chip_7_bally_2,
       video_chip_7_leftbat_2, video_chip_7_rightbat_2;
  wire [31:0] bat_l_32, bat_r_32, multiplexer_2_out, multiplexer_3_out, multiplexer_8_out, multiplexer_9_out,
       y;

  Multiplexer #(.width(32)) multiplexer_1 (.in0({32{1'b0}}), .in1(y), .out(out_6), .sel(comparator_1_eq));  // open: en
  _5_to_32 u_5_to_32_1 (.in_1(in_3), .out_2(y));
  Multiplexer #(.width(32)) multiplexer_2 (
    .in0(bat_l_32), .in1({32{1'b0}}), .out(multiplexer_2_out), .sel(not_1_out));  // open: en
  Comparator #(.width(5)) comparator_1 (.a(in_1), .b(in_2), .eq(comparator_1_eq));  // open: gt, lt
  video_chip video_chip_1 (
    .chipID(in_1), .ballX(in_2), .ballY(in_3), .leftBat(in_4), .rightBat(in_5), .nextChipID(ID1),
    .ballX_2(video_chip_1_ballx_2), .ballY_2(video_chip_1_bally_2), .leftBat_2(video_chip_1_leftbat_2),
    .rightBat_2(video_chip_1_rightbat_2));
  assign out_7 = multiplexer_2_out | multiplexer_3_out;  // OR_Gate or_1, 32 bits wide
  Multiplexer #(.width(32)) multiplexer_3 (
    .in0({32{1'b0}}), .in1(y), .out(multiplexer_3_out), .sel(comparator_2_eq));  // open: en
  not not_1 (not_1_out, comparator_3_eq);
  Comparator #(.width(5)) comparator_2 (.a(ID1), .b(in_2), .eq(comparator_2_eq));  // open: gt, lt
  Comparator #(.width(5)) comparator_3 (.a(ID1), .b(5'b00001), .eq(comparator_3_eq));  // open: gt, lt
  bat_shift bat_shift_1 (.in_1(out_17), .out_2(bat_l_32));
  Multiplexer #(.width(32)) multiplexer_4 (.in0({32{1'b0}}), .in1(y), .out(out_8), .sel(comparator_4_eq));  // open: en
  Comparator #(.width(5)) comparator_4 (.a(ID2), .b(in_2), .eq(comparator_4_eq));  // open: gt, lt
  video_chip video_chip_2 (
    .chipID(ID1), .ballX(video_chip_1_ballx_2), .ballY(video_chip_1_bally_2),
    .leftBat(video_chip_1_leftbat_2), .rightBat(video_chip_1_rightbat_2), .nextChipID(ID2),
    .ballX_2(video_chip_2_ballx_2), .ballY_2(video_chip_2_bally_2), .leftBat_2(video_chip_2_leftbat_2),
    .rightBat_2(video_chip_2_rightbat_2));
  Multiplexer #(.width(32)) multiplexer_5 (.in0({32{1'b0}}), .in1(y), .out(out_9), .sel(comparator_5_eq));  // open: en
  Comparator #(.width(5)) comparator_5 (.a(ID3), .b(in_2), .eq(comparator_5_eq));  // open: gt, lt
  video_chip video_chip_3 (
    .chipID(ID2), .ballX(video_chip_2_ballx_2), .ballY(video_chip_2_bally_2),
    .leftBat(video_chip_2_leftbat_2), .rightBat(video_chip_2_rightbat_2), .nextChipID(ID3),
    .ballX_2(video_chip_3_ballx_2), .ballY_2(video_chip_3_bally_2), .leftBat_2(video_chip_3_leftbat_2),
    .rightBat_2(video_chip_3_rightbat_2));
  Multiplexer #(.width(32)) multiplexer_6 (.in0({32{1'b0}}), .in1(y), .out(out_10), .sel(comparator_6_eq));  // open: en
  video_chip video_chip_4 (
    .chipID(ID3), .ballX(video_chip_3_ballx_2), .ballY(video_chip_3_bally_2),
    .leftBat(video_chip_3_leftbat_2), .rightBat(video_chip_3_rightbat_2), .nextChipID(ID4),
    .ballX_2(video_chip_4_ballx_2), .ballY_2(video_chip_4_bally_2), .leftBat_2(video_chip_4_leftbat_2),
    .rightBat_2(video_chip_4_rightbat_2));
  Comparator #(.width(5)) comparator_6 (.a(ID4), .b(in_2), .eq(comparator_6_eq));  // open: gt, lt
  video_chip video_chip_5 (
    .chipID(ID4), .ballX(video_chip_4_ballx_2), .ballY(video_chip_4_bally_2),
    .leftBat(video_chip_4_leftbat_2), .rightBat(video_chip_4_rightbat_2), .nextChipID(ID5),
    .ballX_2(video_chip_5_ballx_2), .ballY_2(video_chip_5_bally_2), .leftBat_2(video_chip_5_leftbat_2),
    .rightBat_2(video_chip_5_rightbat_2));
  Multiplexer #(.width(32)) multiplexer_7 (.in0({32{1'b0}}), .in1(y), .out(out_11), .sel(comparator_7_eq));  // open: en
  Comparator #(.width(5)) comparator_7 (.a(ID5), .b(in_2), .eq(comparator_7_eq));  // open: gt, lt
  video_chip video_chip_6 (
    .chipID(ID5), .ballX(video_chip_5_ballx_2), .ballY(video_chip_5_bally_2),
    .leftBat(video_chip_5_leftbat_2), .rightBat(video_chip_5_rightbat_2), .nextChipID(ID6),
    .ballX_2(video_chip_6_ballx_2), .ballY_2(video_chip_6_bally_2), .leftBat_2(video_chip_6_leftbat_2),
    .rightBat_2(video_chip_6_rightbat_2));
  assign out_12 = multiplexer_8_out | multiplexer_9_out;  // OR_Gate or_2, 32 bits wide
  Multiplexer #(.width(32)) multiplexer_8 (
    .in0(bat_r_32), .in1({32{1'b0}}), .out(multiplexer_8_out), .sel(not_2_out));  // open: en
  Multiplexer #(.width(32)) multiplexer_9 (
    .in0({32{1'b0}}), .in1(y), .out(multiplexer_9_out), .sel(comparator_8_eq));  // open: en
  Comparator #(.width(5)) comparator_8 (.a(ID6), .b(in_2), .eq(comparator_8_eq));  // open: gt, lt
  Comparator #(.width(5), .mode("unsigned")) comparator_9 (
    .a(ID6), .b(5'b11110), .eq(comparator_9_eq));  // open: gt, lt
  bat_shift bat_shift_2 (.in_1(out_18), .out_2(bat_r_32));
  video_chip video_chip_7 (
    .chipID(ID6), .ballX(video_chip_6_ballx_2), .ballY(video_chip_6_bally_2),
    .leftBat(video_chip_6_leftbat_2), .rightBat(video_chip_6_rightbat_2), .nextChipID(ID7),
    .ballX_2(video_chip_7_ballx_2), .ballY_2(video_chip_7_bally_2), .leftBat_2(video_chip_7_leftbat_2),
    .rightBat_2(video_chip_7_rightbat_2));
  Multiplexer #(.width(32)) multiplexer_10 (
    .in0({32{1'b0}}), .in1(y), .out(out_13), .sel(comparator_10_eq));  // open: en
  not not_2 (not_2_out, comparator_9_eq);
  Comparator #(.width(5)) comparator_10 (.a(ID7), .b(in_2), .eq(comparator_10_eq));  // open: gt, lt
  video_chip video_chip_8 (
    .chipID(ID7), .ballX(video_chip_7_ballx_2), .ballY(video_chip_7_bally_2),
    .leftBat(video_chip_7_leftbat_2), .rightBat(video_chip_7_rightbat_2), .nextChipID(out_14),
    .ballX_2(out_15), .ballY_2(out_16), .leftBat_2(out_17), .rightBat_2(out_18));

  // Other names for the same wires on the sheet: bat_l[4:0] = out_17; bat_r[4:0] = out_18; ID0[4:0] = in_1;
  //   x[4:0] = in_2
endmodule

module inrange (
  input  [4:0] Yball,
  input  [4:0] Ybat,
  input  isTheSameX,
  output exit
);

  wire comparator_1_lt, comparator_2_gt, nor_1_out;
  wire [4:0] adder_1_out;

  // Probe on Yball
  // Probe on Ybat
  // Probe on adder_1_out
  Adder #(.width(5)) adder_1 (.a(5'b00011), .b(Ybat), .out(adder_1_out));  // open: cin, cout
  Comparator #(.width(5)) comparator_1 (.a(Yball), .b(Ybat), .lt(comparator_1_lt));  // open: gt, eq
  Comparator #(.width(5)) comparator_2 (.a(Yball), .b(adder_1_out), .gt(comparator_2_gt));  // open: eq, lt
  nor nor_1 (nor_1_out, comparator_1_lt, comparator_2_gt);
  assign exit = isTheSameX ? nor_1_out : 1'bz;  // Controlled_Buffer controlled_buffer_1
  Pull_Resistor pull_resistor_1 (.node(exit));
endmodule

module reflect (
  input  [2:0] in_1,
  output [2:0] out_2
);

  wire comparator_1_eq;
  wire [2:0] inc_3_1_out_2, not_1_out, not_2_out;

  assign not_1_out = ~in_1;  // NOT_Gate not_1, 3 bits wide
  assign not_2_out = ~in_1;  // NOT_Gate not_2, 3 bits wide
  Comparator #(.width(3)) comparator_1 (.a(3'b100), .b(in_1), .eq(comparator_1_eq));  // open: gt, lt
  inc_3 inc_3_1 (.in_1(not_2_out), .out_2(inc_3_1_out_2));
  switch switch_1 (.in_1(not_1_out), .in_2(comparator_1_eq), .in_3(inc_3_1_out_2), .out_4(out_2));
endmodule

module switch (
  input  [2:0] in_1,
  input  in_2,
  input  [2:0] in_3,
  output [2:0] out_4
);

  wire [2:0] and_1_out, and_2_out;
  wire [2:2] not_1_out;

  not not_1 (not_1_out[2], in_2);
  assign and_1_out = in_1 & {3{not_1_out[2]}};  // AND_Gate and_1, 3 bits wide
  assign and_2_out = {3{in_2}} & in_3;  // AND_Gate and_2, 3 bits wide
  assign out_4 = and_1_out | and_2_out;  // OR_Gate or_1, 3 bits wide
endmodule

module inc_3 (
  input  [2:0] in_1,
  output [2:0] out_2
);

  wire [2:0] and_1_out;

  assign and_1_out = {and_1_out[1:0], 1'b1} & in_1;  // AND_Gate and_1, 3 bits wide
  assign out_2 = in_1 ^ {and_1_out[1:0], 1'b1};  // XOR_Gate xor_1, 3 bits wide
  // also tied to GND on the sheet: and_1_out[2]
endmodule

module kinematic_controller (
  input  [1:0] button_up,
  input  [4:0] leftYin,
  input  reset,
  input  [4:0] in_4,
  input  [4:0] in_5,
  input  [4:0] xball,
  input  [4:0] yball,
  output [4:0] out_8,
  output [4:0] ballX,
  output [4:0] ballY,
  output [4:0] leftYout,
  output [4:0] rightYout,
  output [7:0] vxy,
  output [7:0] scoreA,
  output [7:0] scoreB
);

  wire clock_1_out, clock_2_out, clock_3_out, clock_4_out, controlled_buffer_1_out, counter_1_q, down, init,
       or_1_out, up, x, y;
  wire [4:0] left_bat_temp, multiplexer_1_out, multiplexer_2_out, multiplexer_3_out, multiplexer_4_out, vx,
       vx_temp, vy, vy_temp, xball_t, yball_t;

  kinematics_controller kinematics_controller_1 (.in_1(leftYout), .in_2(up), .in_3(down), .bat_y(left_bat_temp));
  Comparator #(.width(2), .mode("unsigned")) comparator_1 (.a(2'b10), .b(button_up), .gt(up), .lt(down));  // open: eq
  Multiplexer #(.width(5)) multiplexer_1 (
    .in0(ballX), .in1(5'b01010), .out(multiplexer_1_out), .sel(init));  // open: en
  check_hit check_hit_1 (.ball_x(xball_t), .ball_y(yball_t), .x_hit(x), .y_hit(y));
  assign controlled_buffer_1_out = or_1_out ? clock_1_out : 1'bz;  // Controlled_Buffer controlled_buffer_1
  Clock clock_1 (.out(clock_1_out));
  or or_1 (or_1_out, up, down);
  Register #(.width(5)) xreg (.D(multiplexer_1_out), .Q(xball_t), .clk(clock_2_out));  // open: en, clr
  Clock #(.highDuration(2), .lowDuration(2)) clock_2 (.out(clock_2_out));
  Multiplexer #(.width(5)) multiplexer_2 (.in0(vx), .in1({5{1'b1}}), .out(multiplexer_2_out), .sel(init));  // open: en
  Register #(.width(5)) u_vx (.D(multiplexer_2_out), .Q(vx_temp), .clk(clock_3_out));  // open: en, clr
  Clock #(.highDuration(2), .lowDuration(2)) clock_3 (.out(clock_3_out));
  Register scA ();  // open: D, en, Q, clk, clr
  Register #(.width(5)) leftYreg (.D(left_bat_temp), .Q(leftYout), .clk(controlled_buffer_1_out));  // open: en, clr
  Multiplexer #(.width(5)) multiplexer_3 (
    .in0(ballY), .in1(5'b10000), .out(multiplexer_3_out), .sel(init));  // open: en
  Multiplexer #(.width(5)) multiplexer_4 (.in0(vy), .in1({5{1'b1}}), .out(multiplexer_4_out), .sel(init));  // open: en
  Clock clock_4 (.out(clock_4_out));
  Register #(.width(5)) yreg (.D(multiplexer_3_out), .Q(yball_t), .clk(clock_2_out));  // open: en, clr
  Register #(.width(5)) u_vy (.D(multiplexer_4_out), .Q(vy_temp), .clk(clock_3_out));  // open: en, clr
  Register scB ();  // open: D, en, Q, clk, clr
  Register #(.width(5)) rightYreg (.D({5{1'b0}}), .Q(rightYout), .clk(clock_4_out));  // open: en, clr
  ballsmove ballsmove_1 (
    .crash_x(x), .crash_y(y), .vx(vx_temp), .vy(vy_temp), .ball_x(xball_t), .ball_y(yball_t),
    .ball_x_2(ballX), .ball_y_2(ballY), .new_vx(vx), .new_vy(vy));
  Comparator #(.width(1), .mode("unsigned")) comparator_2 (.a(1'b0), .b(counter_1_q), .eq(init));  // open: gt, lt
  Counter #(.width(1), .max('h1)) counter_1 (
    .count(init), .Q(counter_1_q), .clk(clock_4_out));  // open: load, D, carry, clr

  assign out_8 = {5{1'b0}};

  // Other names for the same wires on the sheet: left_bat[4:0] = leftYin; left_bat_out[4:0] = leftYout;
  //   x_ball[4:0] = ballX; y_ball[4:0] = ballY
endmodule

module video_system (
  input  [4:0] in_1,
  input  [4:0] in_2,
  input  [4:0] in_3,
  input  [4:0] in_4,
  input  [4:0] in_5,
  output [31:0] out_6,
  output [31:0] out_7,
  output [31:0] out_8,
  output [31:0] out_9,
  output [31:0] out_10,
  output [31:0] out_11,
  output [31:0] out_12,
  output [31:0] out_13,
  output [31:0] out_14,
  output [31:0] out_15,
  output [31:0] out_16,
  output [31:0] out_17,
  output [31:0] out_18,
  output [31:0] out_19,
  output [31:0] out_20,
  output [31:0] out_21,
  output [31:0] out_22,
  output [31:0] out_23,
  output [31:0] out_24,
  output [31:0] out_25,
  output [31:0] out_26,
  output [31:0] out_27,
  output [31:0] out_28,
  output [31:0] out_29,
  output [31:0] out_30,
  output [31:0] out_31,
  output [31:0] out_32,
  output [31:0] out_33,
  output [31:0] out_34,
  output [31:0] out_35,
  output [31:0] out_36,
  output [31:0] out_37
);

  wire [4:0] video_section_1_out_14, video_section_1_out_15, video_section_1_out_16, video_section_1_out_17,
       video_section_1_out_18, video_section_2_out_14, video_section_2_out_15, video_section_2_out_16,
       video_section_2_out_17, video_section_2_out_18, video_section_3_out_14, video_section_3_out_15,
       video_section_3_out_16, video_section_3_out_17, video_section_3_out_18;

  video_section video_section_1 (
    .in_1(in_1), .in_2(in_2), .in_3(in_3), .in_4(in_4), .in_5(in_5), .out_6(out_6), .out_7(out_7),
    .out_8(out_8), .out_9(out_9), .out_10(out_10), .out_11(out_11), .out_12(out_12), .out_13(out_13),
    .out_14(video_section_1_out_14), .out_15(video_section_1_out_15), .out_16(video_section_1_out_16),
    .out_17(video_section_1_out_17), .out_18(video_section_1_out_18));
  video_section video_section_2 (
    .in_1(video_section_1_out_14), .in_2(video_section_1_out_15), .in_3(video_section_1_out_16),
    .in_4(video_section_1_out_17), .in_5(video_section_1_out_18), .out_6(out_14), .out_7(out_15),
    .out_8(out_16), .out_9(out_17), .out_10(out_18), .out_11(out_19), .out_12(out_20), .out_13(out_21),
    .out_14(video_section_2_out_14), .out_15(video_section_2_out_15), .out_16(video_section_2_out_16),
    .out_17(video_section_2_out_17), .out_18(video_section_2_out_18));
  video_section video_section_3 (
    .in_1(video_section_2_out_14), .in_2(video_section_2_out_15), .in_3(video_section_2_out_16),
    .in_4(video_section_2_out_17), .in_5(video_section_2_out_18), .out_6(out_22), .out_7(out_23),
    .out_8(out_24), .out_9(out_25), .out_10(out_26), .out_11(out_27), .out_12(out_28), .out_13(out_29),
    .out_14(video_section_3_out_14), .out_15(video_section_3_out_15), .out_16(video_section_3_out_16),
    .out_17(video_section_3_out_17), .out_18(video_section_3_out_18));
  video_section video_section_4 (
    .in_1(video_section_3_out_14), .in_2(video_section_3_out_15), .in_3(video_section_3_out_16),
    .in_4(video_section_3_out_17), .in_5(video_section_3_out_18), .out_6(out_30), .out_7(out_31),
    .out_8(out_32), .out_9(out_33), .out_10(out_34), .out_11(out_35), .out_12(out_36), .out_13(out_37));  // open: out_14, out_15, out_16, out_17, out_18

  // Other names for the same wires on the sheet: _0[31:0] = out_6; _1[31:0] = out_7; _2[31:0] = out_8;
  //   _3[31:0] = out_9; _4[31:0] = out_10; _5[31:0] = out_11; _6[31:0] = out_12; _7[31:0] = out_13; _8[31:0] = out_14;
  //   _9[31:0] = out_15; _10[31:0] = out_16; _11[31:0] = out_17; _12[31:0] = out_18; _13[31:0] = out_19;
  //   _14[31:0] = out_20; _15[31:0] = out_21; _16[31:0] = out_22; _17[31:0] = out_23; _18[31:0] = out_24;
  //   _19[31:0] = out_25; _20[31:0] = out_26; _21[31:0] = out_27; _22[31:0] = out_28; _23[31:0] = out_29;
  //   _24[31:0] = out_30; _25[31:0] = out_31; _26[31:0] = out_32; _27[31:0] = out_33; _28[31:0] = out_34;
  //   _29[31:0] = out_35; _30[31:0] = out_36; _31[31:0] = out_37
endmodule

// conv
module _5_to_32 (
  input  [4:0] in_1,
  output [31:0] out_2
);

  Shifter #(.width(32)) shifter_1 (.in(32'h1), .\dist (in_1), .out(out_2));
endmodule

module bat_shift (
  input  [4:0] in_1,
  output [31:0] out_2
);

  wire [31:0] adder_1_out, adder_2_out, n5_to_32_1_out_2, shifter_1_out, shifter_2_out, shifter_3_out;

  _5_to_32 u_5_to_32_1 (.in_1(in_1), .out_2(n5_to_32_1_out_2));
  Shifter #(.width(32)) shifter_1 (.in(n5_to_32_1_out_2), .\dist (5'b00001), .out(shifter_1_out));
  Shifter #(.width(32)) shifter_2 (.in(shifter_1_out), .\dist (5'b00001), .out(shifter_2_out));
  Adder #(.width(32)) adder_1 (.a(shifter_1_out), .b(n5_to_32_1_out_2), .out(adder_1_out));  // open: cin, cout
  Shifter #(.width(32)) shifter_3 (.in(shifter_2_out), .\dist (5'b00001), .out(shifter_3_out));
  Adder #(.width(32)) adder_2 (.a(shifter_2_out), .b(adder_1_out), .out(adder_2_out));  // open: cin, cout
  Adder #(.width(32)) adder_3 (.a(shifter_3_out), .b(adder_2_out), .out(out_2));  // open: cin, cout
endmodule

module kinematics_controller (
  input  [4:0] in_1,
  input  in_2,
  input  in_3,
  output [4:0] bat_y
);

  wire comparator_1_lt, comparator_2_gt, controlled_buffer_1_out, controlled_buffer_2_out;
  wire [4:0] adder_1_out, inc_1_out_2, multiplexer_1_out, multiplexer_2_out;

  // Probe on in_1
  Comparator #(.width(5), .mode("unsigned")) comparator_1 (
    .a(in_1), .b(5'b11100), .lt(comparator_1_lt));  // open: gt, eq
  assign controlled_buffer_1_out = comparator_1_lt ? in_2 : 1'bz;  // Controlled_Buffer controlled_buffer_1
  assign controlled_buffer_2_out = comparator_2_gt ? in_3 : 1'bz;  // Controlled_Buffer controlled_buffer_2
  Comparator #(.width(5), .mode("unsigned")) comparator_2 (
    .a(in_1), .b({5{1'b0}}), .gt(comparator_2_gt));  // open: eq, lt
  Pull_Resistor pull_resistor_1 (.node(controlled_buffer_1_out));
  Pull_Resistor pull_resistor_2 (.node(controlled_buffer_2_out));
  inc inc_1 (.in_1(in_1), .out_2(inc_1_out_2));
  Adder #(.width(5)) adder_1 (.a(in_1), .b({5{1'b1}}), .out(adder_1_out));  // open: cin, cout
  Multiplexer #(.width(5)) multiplexer_1 (
    .in0(in_1), .in1(inc_1_out_2), .out(multiplexer_1_out), .sel(controlled_buffer_1_out));  // open: en
  Multiplexer #(.width(5)) multiplexer_2 (
    .in0(in_1), .in1(adder_1_out), .out(multiplexer_2_out), .sel(controlled_buffer_2_out));  // open: en
  Multiplexer #(.width(5)) multiplexer_3 (
    .in0(multiplexer_1_out), .in1(multiplexer_2_out), .out(bat_y), .sel(controlled_buffer_2_out));  // open: en
endmodule

module leds (
  output [31:0] out_1
);

  wire clock_1_out;

  Clock #(.highDuration(10), .lowDuration(10)) clock_1 (.out(clock_1_out));
  Multiplexer #(.width(32)) multiplexer_1 (
    .in0(32'h55555555), .in1(32'haaaaaaaa), .out(out_1), .sel(clock_1_out));  // open: en
endmodule

module ballsmove (
  input  crash_x,
  input  crash_y,
  input  [4:0] vx,
  input  [4:0] vy,
  input  [4:0] ball_x,
  input  [4:0] ball_y,
  output [4:0] ball_x_2,
  output [4:0] ball_y_2,
  output [4:0] new_vx,
  output [4:0] new_vy
);

  wire [4:0] if_help_1_res, if_help_2_res, inc_2_out_2, neg_vx, not_1_out, not_2_out;

  assign not_1_out = ~vx;  // NOT_Gate not_1, 5 bits wide
  assign not_2_out = ~vy;  // NOT_Gate not_2, 5 bits wide
  if_help if_help_1 (.A(vx), .sel(crash_x), .B(neg_vx), .res(if_help_1_res));
  inc inc_1 (.in_1(not_1_out), .out_2(neg_vx));
  if_help if_help_2 (.A(vy), .sel(crash_y), .B(inc_2_out_2), .res(if_help_2_res));
  inc inc_2 (.in_1(not_2_out), .out_2(inc_2_out_2));
  Adder #(.width(5)) adder_1 (.a(if_help_1_res), .b(ball_x), .out(ball_x_2));  // open: cin, cout
  Adder #(.width(5)) adder_2 (.a(if_help_2_res), .b(ball_y), .out(ball_y_2));  // open: cin, cout
  Multiplexer #(.width(5)) multiplexer_1 (.in0(vx), .in1(neg_vx), .out(new_vx), .sel(crash_x));  // open: en
  Multiplexer #(.width(5)) multiplexer_2 (.in0(vy), .in1(inc_2_out_2), .out(new_vy), .sel(crash_y));  // open: en
endmodule

module if_help (
  input  [4:0] A,
  input  sel,
  input  [4:0] B,
  output [4:0] res
);

  wire [4:0] and_1_out, and_2_out;
  wire [4:4] not_1_out;

  not not_1 (not_1_out[4], sel);
  assign and_1_out = A & {5{not_1_out[4]}};  // AND_Gate and_1, 5 bits wide
  assign and_2_out = {5{sel}} & B;  // AND_Gate and_2, 5 bits wide
  assign res = and_1_out | and_2_out;  // OR_Gate or_1, 5 bits wide
endmodule

module check_hit (
  input  [4:0] ball_x,
  input  [4:0] ball_y,
  output x_hit,
  output y_hit
);

  wire comparator_1_eq, comparator_2_eq, comparator_3_eq, comparator_4_eq;

  Comparator #(.width(5)) comparator_1 (.a({5{1'b0}}), .b(ball_x), .eq(comparator_1_eq));  // open: gt, lt
  Comparator #(.width(5)) comparator_2 (.a({5{1'b1}}), .b(ball_x), .eq(comparator_2_eq));  // open: gt, lt
  Comparator #(.width(5)) comparator_3 (.a({5{1'b0}}), .b(ball_y), .eq(comparator_3_eq));  // open: gt, lt
  Comparator #(.width(5)) comparator_4 (.a({5{1'b1}}), .b(ball_y), .eq(comparator_4_eq));  // open: gt, lt
  or or_1 (x_hit, comparator_1_eq, comparator_2_eq);
  or or_2 (y_hit, comparator_3_eq, comparator_4_eq);
endmodule
